// Logisim project CS131-LAB.circ as structural Verilog: 4 circuits, main circuit Lab02
module Lab02 (
  input  a,
  input  b,
  input  c,
  input  d,
  output f
);

  wire and_1_out, and_2_out, and_3_out, and_4_out, not_1_out, not_2_out, not_3_out, or_1_out;

  and and_1 (and_1_out, c, d);
  or or_1 (or_1_out, a, b);
  not not_1 (not_1_out, b);
  not not_2 (not_2_out, d);
  not not_3 (not_3_out, c);
  and and_2 (and_2_out, b, not_3_out);
  and and_3 (and_3_out, and_1_out, or_1_out);
  and and_4 (and_4_out, not_1_out, c, not_2_out);
  or or_2 (f, and_2_out, and_3_out, and_4_out);

  // Notes on the sheet:
  //   f = bc' + cd(a+b) + b'cd'
endmodule

module Lab03 (
  input  a,
  input  b,
  input  c,
  input  d,
  output f
);

  wire and_1_out, and_2_out, and_3_out, and_4_out, not_1_out, not_2_out, not_3_out;

  not not_1 (not_1_out, b);
  not not_2 (not_2_out, d);
  not not_3 (not_3_out, c);
  and and_1 (and_1_out, a, not_1_out, c);
  and and_2 (and_2_out, b, c, d);
  and and_3 (and_3_out, not_1_out, c, not_2_out);
  and and_4 (and_4_out, b, not_3_out);
  or or_1 (f, and_1_out, and_2_out, and_3_out, and_4_out);
endmodule

module Lab04 (
  input  D,
  input  B,
  input  S,
  input  E,
  input  H
);

  wire and_1_out, and_2_out, and_3_out, and_4_out, not_1_out, not_2_out, not_3_out, not_4_out, or_1_out;

  not not_1 (not_1_out, D);
  not not_2 (not_2_out, B);
  not not_3 (not_3_out, S);
  not not_4 (not_4_out, E);
  and and_1 (and_1_out, B, E, not_3_out);
  and and_2 (and_2_out, not_2_out, S, E);
  and and_3 (and_3_out, not_1_out, E, not_2_out);
  and and_4 (and_4_out, not_4_out, H);
  or or_1 (or_1_out, and_1_out, and_2_out, and_3_out, and_4_out);
  LED led_1 (.in(or_1_out));
endmodule

module Lab04Var (
  input  SeatBelt_B,
  input  Door_D,
  input  Engine_E,
  input  Headlights_H,
  input  Seat_S
);

  wire and_1_out, and_2_out, and_3_out, and_4_out, not_1_out, not_2_out, not_3_out, not_4_out, or_1_out;

  not not_1 (not_1_out, Engine_E);
  not not_2 (not_2_out, Seat_S);
  not not_3 (not_3_out, Door_D);
  not not_4 (not_4_out, SeatBelt_B);
  and and_1 (and_1_out, not_4_out, Seat_S, Engine_E);
  and and_2 (and_2_out, not_1_out, Headlights_H);
  and and_3 (and_3_out, SeatBelt_B, Door_D, not_2_out);
  and and_4 (and_4_out, not_3_out, Engine_E);
  or or_1 (or_1_out, and_1_out, and_2_out, and_3_out, and_4_out);
  LED Buzzer (.in(or_1_out));
endmodule
